// Logisim project ,multi sequencer.circ as structural Verilog: 1 circuit, main circuit main
module main (
  input  [3:0] DR_11_14,
  input  [6:0] SBR_OUTPUT,
  input  CD_10,
  input  CD_9,
  input  BR_8,
  input  BR_7,
  input  AD_6,
  input  AD_5,
  input  AD_4,
  input  AD_3,
  input  AD_2,
  input  AD_1,
  input  AD_0,
  input  [15:0] AC,
  input  [6:0] CAR_OUTPUT,
  input  in_16,
  output [6:0] SBR_INPUT,
  output [6:0] CAR_INPUT,
  output LD_SBR
);

  wire multiplexer_1_out, or_1_out, or_2_out;
  wire [1:0] Input_logic_s1;
  wire [6:0] undriven;

  or or_1 (or_1_out, AC[14], AC[13], AC[12], AC[11], AC[10], AC[9], AC[8], AC[7], AC[6], AC[5], AC[4], AC[3], AC[2], AC[1], AC[0]);
  or or_2 (or_2_out, AC[15], or_1_out);
  Multiplexer #(.select(2)) multiplexer_1 (
    .in0(1'b1), .in1(in_16), .in2(AC[15]), .out(multiplexer_1_out), .sel({CD_9, CD_10}));  // open: in3, en
  INPUTVLOGIC_main Input_logic (
    .I1(BR_8), .I0(BR_7), .T(multiplexer_1_out), .S1(Input_logic_s1[0]), .S0(Input_logic_s1[1]), .L(LD_SBR));
  Multiplexer #(.select(2), .width(7)) multiplexer_2 (
    .in0(SBR_INPUT), .in1({AD_6, AD_5, AD_4, AD_3, AD_2, AD_1, AD_0}), .in2(SBR_OUTPUT),
    .in3({undriven[6], DR_11_14, undriven[1:0]}), .out(CAR_INPUT), .sel(Input_logic_s1));  // open: en
  Adder #(.width(7)) adder_1 (.a(CAR_OUTPUT), .b(7'b0000001), .out(SBR_INPUT));  // open: cin, cout
endmodule
