// Logisim project ALU.circ as structural Verilog: 1 circuit, main circuit main
module main (
  input  DR_i,
  input  AC_i,
  input  AC_i_1,
  input  Bin,
  input  AC_i_1_2,
  input  Cin,
  input  AND,
  input  ADD,
  input  SUB,
  input  OR,
  input  LD,
  input  CLOCK,
  input  DRTAC,
  input  XOR,
  input  CLEAR,
  input  COM,
  input  SHL,
  input  SHR,
  output Cout,
  output Bout,
  output AC_I_2
);

  wire adder_1_out, and_1_out, and_2_out, and_3_out, and_4_out, and_5_out, and_6_out, and_7_out, and_8_out,
       and_9_out, and_10_out, and_11_out, not_1_out, not_2_out, or_1_out, or_2_out, subtractor_1_out,
       xor_1_out;

  not not_1 (not_1_out, AC_i);
  Subtractor #(.width(1)) subtractor_1 (.a(AC_i), .b(DR_i), .out(subtractor_1_out), .bin(Bin), .bout(Bout));
  and and_1 (and_1_out, DRTAC, DR_i);
  Adder #(.width(1)) adder_1 (.a(AC_i), .b(DR_i), .out(adder_1_out), .cin(Cin), .cout(Cout));
  or or_1 (or_1_out, AC_i, DR_i);
  xor xor_1 (xor_1_out, AC_i, DR_i);
  and and_2 (and_2_out, COM, not_1_out);
  and and_3 (and_3_out, SHL, AC_i_1);
  and and_4 (and_4_out, SHR, AC_i_1_2);
  and and_5 (and_5_out, AND, AC_i, DR_i);
  and and_6 (and_6_out, adder_1_out, ADD);
  and and_7 (and_7_out, SUB, subtractor_1_out);
  and and_8 (and_8_out, OR, or_1_out);
  and and_9 (and_9_out, XOR, xor_1_out);
  or or_2 (or_2_out, and_5_out, and_6_out, and_7_out, and_8_out, and_9_out, and_2_out, and_3_out, and_4_out, and_1_out);
  and and_10 (and_10_out, or_2_out, LD);
  not not_2 (not_2_out, or_2_out);
  and and_11 (and_11_out, not_2_out, LD);
  J_K_Flip_Flop j_k_ff_1 (
    .J(and_10_out), .clk(CLOCK), .K(and_11_out), .Q(AC_I_2), .reset(CLEAR));  // open: Qn, preset, en
endmodule
