// Logisim project INPUTVLOGIC.circ as structural Verilog: 1 circuit, main circuit main
module main (
  input  I1,
  input  I0,
  input  T,
  output S1,
  output S0,
  output L
);

  wire and_1_out, and_2_out, not_1_out, not_2_out;

  not not_1 (not_1_out, I1);
  not not_2 (not_2_out, I0);
  and and_1 (and_1_out, I1, I0);
  and and_2 (and_2_out, not_1_out, T);
  and and_3 (L, not_1_out, I0, T);
  or or_1 (S0, and_1_out, and_2_out);

  assign S1 = I1;
endmodule
